# Fritzing sketch SensorAndMotor (saved by Fritzing 1.0.1rc)
breadboards: 1

parts:
  Part1 = Adafruit T-Cobbler Plus [part_number="Adafruit #1989 and #2028"]
  MH-ET_LIVE_ESP32_DEVKIT1 = MH-ET LIVE ESP32 DEVKIT 38 pins
  IC1 = L293D [package=THT]
  DHT1 = DHT11 Humitidy and Temperature Sensor
  M1 = DC Motor [voltage_(max)=6V voltage_(min)=3V]
  R1 = Resistor [tolerance=±5% power=0.25 resistance=220 package=THT]

nets:
  N1: Part1.GND, Part1.GPIO17, Part1.GPIO27, Part1.GPIO22, Part1.SCLK, Part1.EEDAT, Part1.GPIO5, Part1.GPIO6, Part1.RXD, Part1.GPIO18, Part1.GPIO23, Part1.CE1, Part1.+3.3V_2, Part1.GPIO24, Part1.CE0, Part1.EECLK, Part1.GPIO12, IC1.Enable_1, IC1.In_1, IC1.0V, IC1.In_2
  N2: Part1.+5V, IC1.+Vmotor, IC1.+V
  3V3: MH-ET_LIVE_ESP32_DEVKIT1.3V3, DHT1.VDD, R1.Pin_0
  N3: MH-ET_LIVE_ESP32_DEVKIT1.IO27, DHT1.DATA, R1.Pin_1
  N4: MH-ET_LIVE_ESP32_DEVKIT1.GND#70, DHT1.GND
  N5: IC1.Out_1_(_Controlled_by_Enable_1_), M1.pin_1
  N6: IC1.Out_2_(_Controlled_by_Enable_1_), M1.pin_2

custom parts:
  Adafruit T-Cobbler Plus: The Raspberry Pi has landed on the Maker World like a 40-GPIO pinned, quad-USB ported, credit card sized bomb of DIY joy. And while you can use most of our great Model B accessories by hooking up our downgrade cable, its probably a good time to upgrade your set up and accessorize using all of the 40 pins. That's why we now carry the Assembled Adafruit Pi T-Cobbler Plus - Breakout + Cable for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
  MH-ET LIVE ESP32 DEVKIT 38 pins: http://mh.nodebb.com/topic/2/mh-et-live-esp32-devkit
  DHT11 Humitidy and Temperature Sensor: DHT11 Humidity and Temperature Sensor
